# Fritzing sketch auralink_pcb (saved by Fritzing 1.0.5)
circuit board: 12.397cm x 8.04049cm
breadboards: 2

parts:
  ESP32S3-DevKitC-1 = Werner Rothschopf (modified to ESP32-S3-DevKitC dual USB by vanepp Aug 2024)
  100K = Trimmer Potentiometer [maximum_resistance=10kΩ knob_status=50% power=0.5W package=THT]
  5V = female pin header, 2 pins [form="♀ (female)"]
  3_3V = female pin header, 2 pins [form="♀ (female)"]
  GND = female pin header, 2 pins [form="♀ (female)"]
  SPI_TFT_DISPLAY = female pin header, 8 pins [form="♀ (female)"]
  BH1750 = female pin header, 5 pins [form="♀ (female)"]
  BME280 = female pin header, 4 pins [form="♀ (female)"]
  RTC = female pin header, 6 pins [form="♀ (female)"]

nets (from the pcb view):
  N1: ESP32S3-DevKitC-1.Pin_1, ESP32S3-DevKitC-1.Pin_2
  N2: ESP32S3-DevKitC-1.Pin_10, BH1750.pin3, BME280.pin2, RTC.pin4
  N3: ESP32S3-DevKitC-1.Pin_11, BH1750.pin2, BME280.pin1, RTC.pin3
  N4: ESP32S3-DevKitC-1.Pin_16, SPI_TFT_DISPLAY.pin6
  N5: ESP32S3-DevKitC-1.Pin_17, SPI_TFT_DISPLAY.pin5
  N6: ESP32S3-DevKitC-1.Pin_18, SPI_TFT_DISPLAY.pin4
  N7: ESP32S3-DevKitC-1.Pin_19, SPI_TFT_DISPLAY.pin3
  N8: ESP32S3-DevKitC-1.Pin_20, SPI_TFT_DISPLAY.pin2
  N9: ESP32S3-DevKitC-1.Pin_21, 5V.pin1, 5V.pin2
  N10: ESP32S3-DevKitC-1.Pin_22, GND.pin1, GND.pin2, SPI_TFT_DISPLAY.pin7
  N11: 100K.leg1, 100K.wiper, 3_3V.pin1, 3_3V.pin2, SPI_TFT_DISPLAY.pin8, BH1750.pin1, BH1750.pin5, BME280.pin4, RTC.pin2
  N12: 100K.leg2, SPI_TFT_DISPLAY.pin1
  N13: BH1750.pin4, BME280.pin3

custom parts:
  Werner Rothschopf (modified to ESP32-S3-DevKitC dual USB by vanepp Aug 2024): ESP32-S3 ESP32-S3-DevKitC-1 Dual USB development board Pyboard CircuitPython Micropython wifi BLE5.0 ESP32-S3.
